// Logisim project ORT2Project.circ as structural Verilog: 8 circuits, main circuit COMPUTER
module COMPUTER (
);

  wire BTN_RST_out, CLK, cpu_1_inta, interrupt_interface_4_1_p4, interrupt_interface_4_1_p5,
       interrupt_interface_4_1_p6, interrupt_interface_4_1_p7, pull_resistor_3_node, pull_resistor_6_node,
       ram_1_out_8, rst;
  wire [1:0] cpu_1_uext1__0;
  wire [3:0] interrupt_interface_4_1_p1;
  wire [7:0] pull_resistor_2_node, ram_1_out_7;
  wire [15:0] pull_resistor_1_node;

  Button BTN_RST (.out(BTN_RST_out));
  Clock u_CLK (.out(CLK));
  // RisingEdge risingedge_1: pin names not known; wires that end beside it: BTN_RST_out, CLK, rst
  RAM ram_1 (
    .in_1(pull_resistor_1_node), .in_2(CLK), .in_3(pull_resistor_2_node), .in_4(pull_resistor_3_node),
    .in_5(pull_resistor_6_node), .in_6(rst), .out_7(ram_1_out_7), .out_8(ram_1_out_8));
  Pull_Resistor pull_resistor_1 (.node(pull_resistor_1_node));
  Pull_Resistor pull_resistor_2 (.node(pull_resistor_2_node));
  Pull_Resistor pull_resistor_3 (.node(pull_resistor_3_node));
  Pull_Resistor pull_resistor_4 (.node(ram_1_out_7));
  Pull_Resistor pull_resistor_5 (.node(ram_1_out_8));
  Pull_Resistor pull_resistor_6 (.node(pull_resistor_6_node));
  CPU cpu_1 (
    .in_1(rst), .in_2(CLK), .in_3(ram_1_out_8), .in_4(ram_1_out_7), .ABUS(pull_resistor_1_node),
    .DOUTBUS(pull_resistor_2_node), .out_8(pull_resistor_3_node), .out_9(pull_resistor_6_node),
    .inta(cpu_1_inta), .intr3__0(interrupt_interface_4_1_p1), .UEXT1__0(cpu_1_uext1__0));
  // INTERRUPT_INTERFACE_4 interrupt_interface_4_1: pin names not known; wires that end beside it: interrupt_interface_4_1_p1, cpu_1_inta, cpu_1_uext1__0, interrupt_interface_4_1_p4, interrupt_interface_4_1_p5, interrupt_interface_4_1_p6, interrupt_interface_4_1_p7, CLK
  Button BTN_INTR3 (.out(interrupt_interface_4_1_p4));
  Button BTN_INTR2 (.out(interrupt_interface_4_1_p5));
  Button BTN_INTR1 (.out(interrupt_interface_4_1_p6));
  Button BTN_INTR0 (.out(interrupt_interface_4_1_p7));
endmodule

module CPU (
  input  in_1,
  input  in_2,
  input  in_3,
  input  [7:0] in_4,
  input  [3:0] intr3__0,
  output [15:0] ABUS,
  output [7:0] DOUTBUS,
  output out_8,
  output out_9,
  output inta,
  output [1:0] UEXT1__0
);

  wire [3:0] common_1_phaseffbus;
  wire [5:0] common_1_addrbus, pull_resistor_3_node;
  wire [7:0] pull_resistor_6_node;
  wire [14:0] pull_resistor_5_node;
  wire [15:0] A, ALU, B, INTRADDR, PSW;
  wire [19:0] common_1_instrucbus;
  wire [25:0] pull_resistor_7_node;

  COMMON common_1 (
    .CLK(in_2), .RST(in_1), .DIN(in_4), .CMEMBUS(pull_resistor_5_node), .MAR(ABUS), .MDR(DOUTBUS),
    .PHASEFFBUS(common_1_phaseffbus), .INSTRUCBUS(common_1_instrucbus), .ADDRBUS(common_1_addrbus),
    .PSW(PSW), .CREGBUS(pull_resistor_7_node), .CFFBUS(pull_resistor_6_node), .B(B), .A(A),
    .CPSW(pull_resistor_3_node), .ALU(ALU), .IVTPPDSP(INTRADDR));
  Pull_Resistor pull_resistor_1 (.node(common_1_instrucbus));
  Pull_Resistor pull_resistor_2 (.node(common_1_phaseffbus));
  Pull_Resistor pull_resistor_3 (.node(pull_resistor_3_node));
  Pull_Resistor pull_resistor_4 (.node(common_1_addrbus));
  Pull_Resistor pull_resistor_5 (.node(pull_resistor_5_node));
  Pull_Resistor pull_resistor_6 (.node(pull_resistor_6_node));
  Pull_Resistor pull_resistor_7 (.node(pull_resistor_7_node));
  FETCH fetch_1 (
    .CMEMBUS(pull_resistor_5_node), .CFFBUS(pull_resistor_6_node), .CREGBUS(pull_resistor_7_node),
    .rdMEM(out_9), .in_1(in_1), .in_2(in_2), .in_3(in_3), .PHASEFFBUS(common_1_phaseffbus),
    .ADDRBUS(common_1_addrbus), .PSW(PSW), .INSTRUCBUS(common_1_instrucbus));
  ADDR addr_1 (
    .in_1(in_1), .in_2(in_2), .in_3(in_3), .PHASEFFBUS(common_1_phaseffbus),
    .INSTRUCBUS(common_1_instrucbus), .ADDRBUS(common_1_addrbus), .rdMEM(out_9),
    .CMEMBUS(pull_resistor_5_node), .CFFBUS(pull_resistor_6_node), .CREGBUS(pull_resistor_7_node));
  EXEC exec_1 (
    .in_2(in_1), .in_3(in_2), .in_4(in_3), .B(B), .PHASEFFBUS(common_1_phaseffbus),
    .ADDRBUS(common_1_addrbus), .PSW(PSW), .A(A), .ALU(ALU), .CMEMBUS(pull_resistor_5_node),
    .CFFBUS(pull_resistor_6_node), .CREGBUS(pull_resistor_7_node), .CPSW(pull_resistor_3_node),
    .rdMEM(out_9), .wrMEM(out_8), .INSTRUCBUS(common_1_instrucbus));
  INTR intr_1 (
    .in_1(in_1), .in_2(in_2), .in_3(in_3), .ADDIVTP(INTRADDR), .CREGBUS(pull_resistor_7_node), .rdMEM(out_8),
    .wrMEM(out_9), .UEXT1__0(UEXT1__0), .inta(inta), .PHASEFFBUS(common_1_phaseffbus), .PSW(PSW),
    .intr(intr3__0), .INSTRUCBUS(common_1_instrucbus), .CMEMBUS(pull_resistor_5_node),
    .CFFBUS(pull_resistor_6_node));

  // Other names for the same wires on the sheet: CLK = in_2; DIN7__0[7:0] = in_4; FCBUS = in_3; MAR[15:0] = ABUS;
  //   MDR[7:0] = DOUTBUS; RD = out_9; rst = in_1; WR = out_8
endmodule

module COMMON (
  input  CLK,
  input  RST,
  input  [7:0] DIN,
  input  [15:0] ALU,
  input  [15:0] IVTPPDSP,
  input  [14:0] CMEMBUS,
  input  [7:0] CFFBUS,
  input  [25:0] CREGBUS,
  input  [5:0] CPSW,
  output [15:0] MAR,
  output [15:0] A,
  output [7:0] MDR,
  output [3:0] PHASEFFBUS,
  output [19:0] INSTRUCBUS,
  output [5:0] ADDRBUS,
  output [15:0] PSW,
  output [15:0] B
);

  wire ADRINST, adrinst_t, and_1_out, and_3_out, and_4_out, and_5_out, and_6_out, and_7_out, and_8_out,
       and_9_out, and_10_out, and_11_out, and_12_out, and_13_out, and_14_out, and_15_out, and_16_out,
       and_18_out, and_20_out, and_21_out, and_22_out, and_23_out, and_24_out, bezadrinst, branchinst, C16,
       dc4_16_5_p3, jmpinst, LOGINSTR, mp2_4b_1_p3, mp2_8b_1_p3, mp4_4b_1_p6, mp4_16b_1_p5, mp8_8b_1_p8,
       mp8_16b_1_p8, not_1_out, not_4_out, not_7_out, or_2_out, or_3_out, or_4_out, or_5_out, or_6_out,
       or_7_out, or_8_out, or_9_out, or_11_out, rsff_2_p4, rsff_2_p5, rsff_3_p4, rsff_4_p4, rsff_5_p4,
       rsff_7_p3, rsff_7_p4, rsff_8_p4, rsff_9_p3, rsff_9_p4, rsff_10_p4, SC16, SCN;
  wire [3:0] IR27__24, mp2_4b_2_p3, SCN4__0;
  wire [4:0] SC4__0;
  wire [7:0] DWH, DWL, IR7__0, IR15__8, IR23__16;
  wire [7:4] IR31__24;
  wire [10:0] reg16_1_p3;
  wire [15:0] ADDBRANCH, ADDPCREL15__0, GPR15__0, mp8_16b_2_p8, PC15__0, SP15__0;

  // REG8_LD reg8_ld_1: pin names not known; wires that end beside it: CLK, MDR, IR23__16, CREGBUS[6]
  // DC4_16 dc4_16_1: pin names not known; wires that end beside it: IR31__24, PSW[0], bezadrinst, branchinst, jmpinst, adrinst_t
  // DC4_16 dc4_16_2: pin names not known; wires that end beside it: IR27__24, branchinst, INSTRUCBUS[7], INSTRUCBUS[8], INSTRUCBUS[9], INSTRUCBUS[10], INSTRUCBUS[11], INSTRUCBUS[12]
  // MP4_16b mp4_16b_1: pin names not known; wires that end beside it: CREGBUS[9], CREGBUS[8], {IR7__0, IR15__8}, GPR15__0, mp4_16b_1_p5, {DWH, DWL}, 1'b1
  // REG16_INC_LD reg16_inc_ld_1: pin names not known; wires that end beside it: CLK, mp4_16b_1_p5, B, CREGBUS[0], CREGBUS[22]
  // MP8_16b mp8_16b_1: pin names not known; wires that end beside it: CMEMBUS[7], CMEMBUS[6], CMEMBUS[5], PC15__0, {IR7__0, IR15__8}, B, GPR15__0, mp8_16b_1_p8, ADDPCREL15__0, SP15__0, IVTPPDSP, 1'b1
  // REG16_INC_LD reg16_inc_ld_2: pin names not known; wires that end beside it: CLK, mp8_16b_1_p8, MAR, CMEMBUS[0], CMEMBUS[1]
  // REG8_LD reg8_ld_2: pin names not known; wires that end beside it: CLK, MDR, IR15__8, CREGBUS[5]
  // ADD16 add16_1: pin names not known; wires that end beside it: {{9{IR15__8[7]}}, IR15__8[6:0]}, ADDPCREL15__0, PC15__0
  // REG8_LD reg8_ld_3: pin names not known; wires that end beside it: CLK, MDR, {IR31__24, IR27__24}, CREGBUS[7]
  // DC4_16 dc4_16_3: pin names not known; wires that end beside it: IR27__24, bezadrinst, INSTRUCBUS[0], INSTRUCBUS[1], INSTRUCBUS[2], INSTRUCBUS[3], INSTRUCBUS[4], INSTRUCBUS[5], INSTRUCBUS[6]
  // DC4_16 dc4_16_4: pin names not known; wires that end beside it: IR27__24, jmpinst, INSTRUCBUS[13], INSTRUCBUS[14]
  // REG8_LD reg8_ld_4: pin names not known; wires that end beside it: CLK, MDR, DWH, CREGBUS[3]
  // MP2_8b mp2_8b_1: pin names not known; wires that end beside it: CMEMBUS[11], GPR15__0[15:8], mp2_8b_1_p3, GPR15__0[7:0], 1'b1
  // MP8_8b mp8_8b_1: pin names not known; wires that end beside it: CMEMBUS[10], CMEMBUS[9], CMEMBUS[8], DIN, A[7:0], A[15:8], PC15__0[15:8], mp8_8b_1_p8, PC15__0[7:0], {PSW[15], {7{1'b0}}}, {3'b000, PSW[4:0]}, mp2_8b_1_p3, 1'b1
  // REG8_LD reg8_ld_5: pin names not known; wires that end beside it: CLK, mp8_8b_1_p8, MDR, CMEMBUS[2]
  // REG8_LD reg8_ld_6: pin names not known; wires that end beside it: CLK, MDR, IR7__0, CREGBUS[4]
  // ADD16 add16_2: pin names not known; wires that end beside it: {{9{IR23__16[7]}}, IR23__16[6:0]}, ADDBRANCH, PC15__0
  // REG8_LD reg8_ld_7: pin names not known; wires that end beside it: CLK, MDR, DWL, CREGBUS[2]
  // DC4_16 dc4_16_5: pin names not known; wires that end beside it: IR27__24, adrinst_t, dc4_16_5_p3, INSTRUCBUS[15], INSTRUCBUS[16], INSTRUCBUS[17], dc4_16_5_p3, INSTRUCBUS[18], INSTRUCBUS[19]
  // DC4_16 dc4_16_6: pin names not known; wires that end beside it: IR23__16[7:4], adrinst_t, ADDRBUS[0], ADDRBUS[1], ADDRBUS[2], ADDRBUS[3], ADDRBUS[4], ADDRBUS[5]
  not not_1 (not_1_out, RST);
  // RSFF rsff_1: pin names not known; wires that end beside it: CFFBUS[1], CLK, CFFBUS[0], not_1_out, PHASEFFBUS[0]
  // RSFF rsff_2: pin names not known; wires that end beside it: CFFBUS[3], CLK, CFFBUS[2], rsff_2_p4, rsff_2_p5, PHASEFFBUS[1]
  not not_2 (rsff_2_p5, RST);
  and and_1 (and_1_out, DWL[7], INSTRUCBUS[2]);
  // MP4_4b mp4_4b_1: pin names not known; wires that end beside it: rsff_2_p4, CREGBUS[1], CMEMBUS[3], IR23__16[3:0], 4'b0010, mp4_4b_1_p6, 4'b0000, 1'b1
  // MP2_4b mp2_4b_1: pin names not known; wires that end beside it: CREGBUS[17], SC4__0[3:0], mp2_4b_1_p3, SCN4__0, 1'b1
  // REG5_CL_INC reg5_cl_inc_1: pin names not known; wires that end beside it: CREGBUS[12], CLK, SC4__0, CREGBUS[14]
  and and_2 (SC16, SC4__0[4], ~SC4__0[3], ~SC4__0[2], ~SC4__0[1], ~SC4__0[0]);  // AND_Gate
  or or_1 (LOGINSTR, INSTRUCBUS[3], INSTRUCBUS[4]);
  and and_3 (and_3_out, DWL[1], INSTRUCBUS[2]);
  and and_4 (and_4_out, ~A[0], ~A[1], ~A[2], ~A[3], ~A[4], ~A[5], ~A[6], ~A[7], ~A[8], ~A[9], ~A[10], ~A[11], ~A[12], ~A[13], ~A[14], ~A[15]);  // AND_Gate
  or or_2 (or_2_out, ADRINST, LOGINSTR);
  and and_5 (and_5_out, ~ALU[15], ~B[15], A[15]);  // AND_Gate
  or or_3 (or_3_out, and_5_out, and_6_out);
  and and_6 (and_6_out, ALU[15], B[15], ~A[15]);  // AND_Gate
  // MP2_4b mp2_4b_2: pin names not known; wires that end beside it: CREGBUS[13], mp4_4b_1_p6, mp2_4b_2_p3, mp2_4b_1_p3, 1'b1
  // RSFF rsff_3: pin names not known; wires that end beside it: CFFBUS[5], CLK, CFFBUS[4], rsff_3_p4, PHASEFFBUS[2]
  not not_3 (rsff_3_p4, RST);
  or or_4 (or_4_out, ADRINST, LOGINSTR);
  and and_7 (and_7_out, or_4_out, and_4_out);
  and and_8 (and_8_out, DWL[2], INSTRUCBUS[2]);
  or or_5 (or_5_out, and_8_out, and_9_out);
  and and_9 (and_9_out, or_2_out, A[15]);
  and and_10 (and_10_out, DWL[3], INSTRUCBUS[2]);
  and and_11 (and_11_out, INSTRUCBUS[17], or_3_out);
  not not_4 (not_4_out, and_1_out);
  or or_6 (or_6_out, and_3_out, and_7_out);
  or or_7 (or_7_out, and_10_out, and_11_out);
  // RSFF rsff_4: pin names not known; wires that end beside it: not_4_out, CLK, and_1_out, rsff_4_p4, PSW[15]
  not not_5 (rsff_4_p4, RST);
  GPR16x16N gpr16x16n_1 (
    .DI15__0(mp8_16b_2_p8), .A3__0(mp2_4b_2_p3), .WR(or_9_out), .CLK(CLK), .incPC(CMEMBUS[4]),
    .DO15__0(GPR15__0), .DO15__0_2(PC15__0), .rst(RST), .DO15__0_3(A), .DO15__0_4(SP15__0),
    .incSP(CREGBUS[24]), .decSP(CREGBUS[10]), .decA(CREGBUS[23]), .slA(CREGBUS[11]), .rolcA(INSTRUCBUS[4]));  // open: C
  // REG16 reg16_1: pin names not known; wires that end beside it: CLK, 16'hf, {reg16_1_p3, SCN, SCN4__0}, CREGBUS[16], CREGBUS[15]
  and and_12 (and_12_out, ~DWL[0], INSTRUCBUS[2], CPSW[5]);  // AND_Gate
  or or_8 (or_8_out, and_12_out, CPSW[0]);
  and and_13 (and_13_out, DWL[0], INSTRUCBUS[2], CPSW[5]);
  and and_14 (and_14_out, ~or_5_out, CPSW[2]);  // AND_Gate
  and and_15 (and_15_out, or_5_out, CPSW[2]);
  // MP8_16b mp8_16b_2: pin names not known; wires that end beside it: CREGBUS[20], CREGBUS[19], CREGBUS[18], B, A, ALU, ADDBRANCH, mp8_16b_2_p8, {IR15__8, IR23__16}, {DWH, DWL}, 1'b1
  // RSFF rsff_5: pin names not known; wires that end beside it: CFFBUS[7], CLK, CFFBUS[6], rsff_5_p4, PHASEFFBUS[3]
  not not_6 (rsff_5_p4, RST);
  not not_7 (not_7_out, RST);
  // RSFF rsff_6: pin names not known; wires that end beside it: or_8_out, CLK, and_13_out, not_7_out, PSW[0]
  and and_16 (and_16_out, ~or_6_out, CPSW[1]);  // AND_Gate
  // RSFF rsff_7: pin names not known; wires that end beside it: and_16_out, CLK, rsff_7_p3, rsff_7_p4, PSW[1]
  and and_17 (rsff_7_p3, or_6_out, CPSW[1]);
  not not_8 (rsff_7_p4, RST);
  // RSFF rsff_8: pin names not known; wires that end beside it: and_14_out, CLK, and_15_out, rsff_8_p4, PSW[2]
  not not_9 (rsff_8_p4, RST);
  and and_18 (and_18_out, ~or_7_out, CPSW[3]);  // AND_Gate
  // RSFF rsff_9: pin names not known; wires that end beside it: and_18_out, CLK, rsff_9_p3, rsff_9_p4, PSW[3]
  not not_10 (rsff_9_p4, RST);
  and and_19 (rsff_9_p3, or_7_out, CPSW[3]);
  or or_9 (or_9_out, CREGBUS[21], CREGBUS[1], CMEMBUS[3]);
  or or_10 (ADRINST, INSTRUCBUS[15], INSTRUCBUS[19], INSTRUCBUS[17]);
  and and_20 (and_20_out, DWL[4], INSTRUCBUS[2]);
  and and_21 (and_21_out, A[15], LOGINSTR);
  and and_22 (and_22_out, INSTRUCBUS[17], C16);
  or or_11 (or_11_out, and_20_out, and_21_out, and_22_out);
  and and_23 (and_23_out, ~or_11_out, CPSW[2]);  // AND_Gate
  and and_24 (and_24_out, or_11_out, CPSW[2]);
  // RSFF rsff_10: pin names not known; wires that end beside it: and_23_out, CLK, and_24_out, rsff_10_p4, PSW[4]
  not not_11 (rsff_10_p4, RST);

  assign PSW[14:5] = {10{1'b0}};

  // Other names for the same wires on the sheet: SCN4__0[4] = SCN; MDR0 = DWL[0]; MDR1 = DWL[1]; MDR2 = DWL[2];
  //   MDR3 = DWL[3]; MDR4 = DWL[4]; MDR15 = DWL[7]; A15__0[15:0] = A; immed = ADDRBUS[0]; memdir = ADDRBUS[1];
  //   regdir = ADDRBUS[2]; memind = ADDRBUS[3]; postincr = ADDRBUS[4]; pcrelpom = ADDRBUS[5]; ALU15__0[15:0] = ALU;
  //   B15__0[15:0] = B; stFETCH = CFFBUS[0]; clFETCH = CFFBUS[1]; stADDR = CFFBUS[2]; clADDR = CFFBUS[3];
  //   stEXEC = CFFBUS[4]; clEXEC = CFFBUS[5]; stINTR = CFFBUS[6]; clINTR = CFFBUS[7]; ldMAR = CMEMBUS[0];
  //   incMAR = CMEMBUS[1]; ldMDR = CMEMBUS[2]; ldPC = CMEMBUS[3]; incPC = CMEMBUS[4]; mxMAR0 = CMEMBUS[5];
  //   mxMAR1 = CMEMBUS[6]; mxMAR2 = CMEMBUS[7]; mxMDR0 = CMEMBUS[8]; mxMDR1 = CMEMBUS[9]; mxMDR2 = CMEMBUS[10];
  //   mxMDRGPR = CMEMBUS[11]; clPSWSTART = CPSW[0]; ldZ = CPSW[1]; ldN = CPSW[2]; ldV = CPSW[3]; ldC = CPSW[4];
  //   ldSTART = CPSW[5]; ldB = CREGBUS[0]; ldA = CREGBUS[1]; ldDWL = CREGBUS[2]; ldDWH = CREGBUS[3];
  //   ldIR7__0 = CREGBUS[4]; ldIR15__8 = CREGBUS[5]; ldIR23__16 = CREGBUS[6]; ldIR31__24 = CREGBUS[7];
  //   mxB0 = CREGBUS[8]; mxB1 = CREGBUS[9]; decSP = CREGBUS[10]; slA = CREGBUS[11]; clSC = CREGBUS[12];
  //   mxSC1 = CREGBUS[13]; incSC = CREGBUS[14]; decSC = CREGBUS[15]; ldSCN = CREGBUS[16]; mxSC2 = CREGBUS[17];
  //   mxGPR0 = CREGBUS[18]; mxGPR1 = CREGBUS[19]; mxGPR2 = CREGBUS[20]; wrGPR = CREGBUS[21]; incB = CREGBUS[22];
  //   decA = CREGBUS[23]; incSP = CREGBUS[24]; Din7__0[7:0] = DIN; ENTRADDR15__0[15:0] = IVTPPDSP;
  //   HALT = INSTRUCBUS[0]; RTS = INSTRUCBUS[1]; RTI = INSTRUCBUS[2]; ASL = INSTRUCBUS[3]; ROLC = INSTRUCBUS[4];
  //   PUSHGPR = INSTRUCBUS[5]; POPGPR = INSTRUCBUS[6]; BLSS = INSTRUCBUS[7]; BNCR = INSTRUCBUS[8];
  //   BGRTU = INSTRUCBUS[9]; BNEG = INSTRUCBUS[10]; JLEQ = INSTRUCBUS[11]; LOOPGRE = INSTRUCBUS[12];
  //   JMP = INSTRUCBUS[13]; JSR = INSTRUCBUS[14]; LD = INSTRUCBUS[15]; ST = INSTRUCBUS[16]; SUB = INSTRUCBUS[17];
  //   AND = INSTRUCBUS[18]; NOT = INSTRUCBUS[19]; IR31__24[3:0] = IR27__24; MAR15__0[15:0] = MAR; MDR7__0[7:0] = MDR;
  //   FETCH = PHASEFFBUS[0]; ADDR = PHASEFFBUS[1]; EXEC = PHASEFFBUS[2]; INTR = PHASEFFBUS[3];
  //   PSW15__0 (some bits) = {PSW[15], PSW[4:0]}; PSWSTART = PSW[0]; PSWZ = PSW[1]; PSWN = PSW[2]; PSWV = PSW[3];
  //   PSWC = PSW[4]; PSWI = PSW[15]

  // Notes on the sheet:
  //   Sabirac
  //   Instrukcijski registar
  //   Pomocni registri
  //   MAR
  //   Dekoderi za prepoznavanje instrukcije na osnovu sadrzaja registra IR23..16
  //   MDR
  //   Dekoderi za prepoznavanje nacina adresiranja
  //   FF za pokretanje FETCH, ADDR, EXEC i INTR faze izvršavanja instrukcije
  //   Registarski fajl
  //   Programska statusna reč (PSW)
endmodule

module FETCH (
  input  in_1,
  input  in_2,
  input  in_3,
  input  [3:0] PHASEFFBUS,
  input  [19:0] INSTRUCBUS,
  input  [5:0] ADDRBUS,
  input  [15:0] PSW,
  output [14:0] CMEMBUS,
  output [7:0] CFFBUS,
  output [25:0] CREGBUS,
  output rdMEM
);

  wire addr2, addr3, addr_t, adr4, and_4_out, and_5_out, and_6_out, and_7_out, and_8_out, and_9_out,
       and_10_out, and_11_out, and_12_out, and_13_out, bezadr1, bradr2, bradr3, brbezadr1, brcnd, brgrinst,
       brjmp2, brjmp3, brnotfcmem, bruncnd, clFETCH, grinst, incPC, jmp2, jmp3, ldIR7__0, ldIR15__8,
       ldIR23__16, ldIR31__24, ldMAR, ldMDR, not_1_out, not_3_out, not_4_out, not_5_out, notPSWSTandFETCH,
       or_4_out, or_7_out, or_8_out, rdMEM_t, reg5_cl_inc_ld_1_p5, reg5_cl_inc_ld_1_p6, stADDR, stEXEC;
  wire [4:0] reg5_cl_inc_ld_1_p3, reg5_cl_inc_ld_1_p4;
  wire [23:11] rom_1_dout;

  or or_1 (bezadr1, INSTRUCBUS[3], INSTRUCBUS[1], INSTRUCBUS[4], INSTRUCBUS[0], INSTRUCBUS[5], INSTRUCBUS[2], INSTRUCBUS[6]);
  or or_2 (jmp3, INSTRUCBUS[11], INSTRUCBUS[12], INSTRUCBUS[13], INSTRUCBUS[14]);
  not not_1 (not_1_out, in_1);
  // REG5_CL_INC_LD reg5_cl_inc_ld_1: pin names not known; wires that end beside it: in_2, not_1_out, reg5_cl_inc_ld_1_p3, reg5_cl_inc_ld_1_p4, reg5_cl_inc_ld_1_p5, reg5_cl_inc_ld_1_p6
  not not_2 (reg5_cl_inc_ld_1_p6, reg5_cl_inc_ld_1_p5);
  ROM rom_1 (
    .A4__0(reg5_cl_inc_ld_1_p4), .CS(1'b1),
    .DOUT({rom_1_dout[23:21], reg5_cl_inc_ld_1_p3, rom_1_dout[15:11], stEXEC, stADDR, clFETCH, ldIR7__0, ldIR15__8, ldIR23__16, ldIR31__24, ldMDR, rdMEM_t, incPC, ldMAR}));
  // DC4_16 dc4_16_1: pin names not known; wires that end beside it: rom_1_dout[15:12], 1'b1, brgrinst, bruncnd, notPSWSTandFETCH, brbezadr1, brjmp2, bradr2, brjmp3, bradr3, brnotfcmem
  or or_3 (reg5_cl_inc_ld_1_p5, bruncnd, brcnd);
  or or_4 (or_4_out, ADDRBUS[4], ADDRBUS[2]);
  or or_5 (addr_t, INSTRUCBUS[15], INSTRUCBUS[16], INSTRUCBUS[19], INSTRUCBUS[18], INSTRUCBUS[17]);
  and and_1 (addr3, ADDRBUS[5], addr_t);
  and and_2 (addr2, addr_t, or_4_out);
  or or_6 (jmp2, INSTRUCBUS[7], INSTRUCBUS[8], INSTRUCBUS[9], INSTRUCBUS[10]);
  or or_7 (or_7_out, ADDRBUS[0], ADDRBUS[1], ADDRBUS[3]);
  not not_3 (not_3_out, PHASEFFBUS[0]);
  not not_4 (not_4_out, PSW[0]);
  or or_8 (or_8_out, not_3_out, not_4_out);
  not not_5 (not_5_out, in_3);
  and and_3 (adr4, or_7_out, addr_t);
  and and_4 (and_4_out, or_8_out, notPSWSTandFETCH);
  and and_5 (and_5_out, brbezadr1, bezadr1);
  and and_6 (and_6_out, brjmp2, jmp2);
  and and_7 (and_7_out, bradr2, addr2);
  and and_8 (and_8_out, brgrinst, grinst);
  and and_9 (and_9_out, brjmp3, jmp3);
  and and_10 (and_10_out, bradr3, addr3);
  and and_11 (and_11_out, brnotfcmem, not_5_out);
  or or_9 (brcnd, and_4_out, and_5_out, and_6_out, and_7_out, and_8_out, and_9_out, and_10_out, and_11_out);
  and and_12 (and_12_out, ~jmp2, ~addr_t, ~addr3, ~bezadr1, ~addr2, ~adr4, ~jmp3);  // AND_Gate
  and and_13 (and_13_out, INSTRUCBUS[16], ADDRBUS[0]);
  or or_10 (grinst, and_12_out, and_13_out);
  assign CMEMBUS[0] = ldMAR ? 1'b1 : 1'bz;  // Controlled_Buffer controlled_buffer_1
  assign CMEMBUS[2] = ldMDR ? 1'b1 : 1'bz;  // Controlled_Buffer controlled_buffer_2
  assign CMEMBUS[4] = incPC ? 1'b1 : 1'bz;  // Controlled_Buffer controlled_buffer_3
  assign CFFBUS[1] = clFETCH ? 1'b1 : 1'bz;  // Controlled_Buffer controlled_buffer_4
  assign CFFBUS[2] = stADDR ? 1'b1 : 1'bz;  // Controlled_Buffer controlled_buffer_5
  assign CFFBUS[4] = stEXEC ? 1'b1 : 1'bz;  // Controlled_Buffer controlled_buffer_6
  assign CREGBUS[5] = ldIR15__8 ? 1'b1 : 1'bz;  // Controlled_Buffer controlled_buffer_7
  assign CREGBUS[6] = ldIR23__16 ? 1'b1 : 1'bz;  // Controlled_Buffer controlled_buffer_8
  assign CREGBUS[4] = ldIR7__0 ? 1'b1 : 1'bz;  // Controlled_Buffer controlled_buffer_9
  assign CREGBUS[7] = ldIR31__24 ? 1'b1 : 1'bz;  // Controlled_Buffer controlled_buffer_10
  assign rdMEM = rdMEM_t ? 1'b1 : 1'bz;  // Controlled_Buffer controlled_buffer_11

  // Other names for the same wires on the sheet: immed = ADDRBUS[0]; memdir = ADDRBUS[1]; regdir = ADDRBUS[2];
  //   memind = ADDRBUS[3]; postincr = ADDRBUS[4]; pcrelpom = ADDRBUS[5]; CLK = in_2; FCBUS = in_3;
  //   HALT = INSTRUCBUS[0]; RTS = INSTRUCBUS[1]; RTI = INSTRUCBUS[2]; ASL = INSTRUCBUS[3]; ROLC = INSTRUCBUS[4];
  //   PUSHGPR = INSTRUCBUS[5]; POPGPR = INSTRUCBUS[6]; BLSS = INSTRUCBUS[7]; BNCR = INSTRUCBUS[8];
  //   BGRTU = INSTRUCBUS[9]; BNEG = INSTRUCBUS[10]; JLEQ = INSTRUCBUS[11]; LOOPGRE = INSTRUCBUS[12];
  //   JMP = INSTRUCBUS[13]; JSR = INSTRUCBUS[14]; LD = INSTRUCBUS[15]; ST = INSTRUCBUS[16]; SUB = INSTRUCBUS[17];
  //   AND = INSTRUCBUS[18]; NOT = INSTRUCBUS[19]; FETCH = PHASEFFBUS[0]; ADDR = PHASEFFBUS[1]; EXEC = PHASEFFBUS[2];
  //   INTR = PHASEFFBUS[3]; PSWSTART = PSW[0]; rst = in_1

  // Notes on the sheet:
  //   Operaciona jedinica
  //   Kontrolna jedinica
endmodule

module ADDR (
  input  in_1,
  input  in_2,
  input  in_3,
  input  [3:0] PHASEFFBUS,
  input  [19:0] INSTRUCBUS,
  input  [5:0] ADDRBUS,
  output [14:0] CMEMBUS,
  output [7:0] CFFBUS,
  output [25:0] CREGBUS,
  output rdMEM
);

  wire and_1_out, and_2_out, and_3_out, bradr, brcnd, brnotADDR, brnotfcbus, brSTORE, bruncnd, clADDR, incB,
       incMAR, ldB, ldDWH, ldDWL, ldMAR, ldMDR, mxB0, mxB1, mxMAR0, mxMAR1, mxMAR2, not_1_out, not_3_out,
       not_4_out, rdMEM_t, reg5_cl_inc_ld_1_p6, reg5_cl_inc_ld_1_p7, stEXEC, wrGPR;
  wire [2:0] mp2_8b_1_p2_2;
  wire [4:0] kmadr5_1_adr4__0, mp2_8b_1_p2, reg5_cl_inc_ld_1_p5, rom32x24_1_dout;
  wire [18:16] rom32x24_1_dout_2;

  not not_1 (not_1_out, in_1);
  KMADR5 kmadr5_1 (
    .immed(ADDRBUS[0]), .memdir(ADDRBUS[1]), .regdir(ADDRBUS[2]), .memind(ADDRBUS[3]), .postincr(ADDRBUS[4]),
    .pcrelpom(ADDRBUS[5]), .Adr4__0(kmadr5_1_adr4__0));
  // MP2_8b mp2_8b_1: pin names not known; wires that end beside it: bradr, {mp2_8b_1_p2_2, mp2_8b_1_p2}, 3'b000, 1'b1
  // REG5_CL_INC_LD reg5_cl_inc_ld_1: pin names not known; wires that end beside it: 1'b0, in_2, not_1_out, mp2_8b_1_p2, reg5_cl_inc_ld_1_p5, reg5_cl_inc_ld_1_p6, reg5_cl_inc_ld_1_p7
  not not_2 (reg5_cl_inc_ld_1_p7, reg5_cl_inc_ld_1_p6);
  ROM32x24 rom32x24_1 (
    .A4__0(reg5_cl_inc_ld_1_p5), .CS(1'b1),
    .DOUT({rom32x24_1_dout, rom32x24_1_dout_2, stEXEC, clADDR, mxMAR2, wrGPR, incB, mxMAR1, mxB1, ldDWH, incMAR, ldDWL, ldMDR, rdMEM_t, mxB0, mxMAR0, ldMAR, ldB}));
  // DC3_8 dc3_8_1: pin names not known; wires that end beside it: rom32x24_1_dout_2, 1'b1, bruncnd, brnotADDR, brSTORE, brnotfcbus, bradr
  or or_1 (reg5_cl_inc_ld_1_p6, bruncnd, brcnd, bradr);
  not not_3 (not_3_out, PHASEFFBUS[1]);
  not not_4 (not_4_out, in_3);
  and and_1 (and_1_out, not_3_out, brnotADDR);
  and and_2 (and_2_out, INSTRUCBUS[16], brSTORE);
  and and_3 (and_3_out, brnotfcbus, not_4_out);
  or or_2 (brcnd, and_1_out, and_2_out, and_3_out);
  assign CREGBUS[3] = ldDWH ? 1'b1 : 1'bz;  // Controlled_Buffer controlled_buffer_1
  assign CREGBUS[9] = mxB1 ? 1'b1 : 1'bz;  // Controlled_Buffer controlled_buffer_2
  assign CMEMBUS[1] = incMAR ? 1'b1 : 1'bz;  // Controlled_Buffer controlled_buffer_3
  assign CMEMBUS[2] = ldMDR ? 1'b1 : 1'bz;  // Controlled_Buffer controlled_buffer_4
  assign CMEMBUS[5] = mxMAR0 ? 1'b1 : 1'bz;  // Controlled_Buffer controlled_buffer_5
  assign CMEMBUS[6] = mxMAR1 ? 1'b1 : 1'bz;  // Controlled_Buffer controlled_buffer_6
  assign CMEMBUS[7] = mxMAR2 ? 1'b1 : 1'bz;  // Controlled_Buffer controlled_buffer_7
  assign CFFBUS[3] = clADDR ? 1'b1 : 1'bz;  // Controlled_Buffer controlled_buffer_8
  assign CFFBUS[4] = stEXEC ? 1'b1 : 1'bz;  // Controlled_Buffer controlled_buffer_9
  assign CREGBUS[0] = ldB ? 1'b1 : 1'bz;  // Controlled_Buffer controlled_buffer_10
  assign CREGBUS[2] = ldDWL ? 1'b1 : 1'bz;  // Controlled_Buffer controlled_buffer_11
  assign CREGBUS[8] = mxB0 ? 1'b1 : 1'bz;  // Controlled_Buffer controlled_buffer_12
  assign CREGBUS[21] = wrGPR ? 1'b1 : 1'bz;  // Controlled_Buffer controlled_buffer_13
  assign CMEMBUS[0] = ldMAR ? 1'b1 : 1'bz;  // Controlled_Buffer controlled_buffer_14
  assign CREGBUS[22] = incB ? 1'b1 : 1'bz;  // Controlled_Buffer controlled_buffer_15
  assign rdMEM = rdMEM_t ? 1'b1 : 1'bz;  // Controlled_Buffer controlled_buffer_16

  // Other names for the same wires on the sheet: immed = ADDRBUS[0]; memdir = ADDRBUS[1]; regdir = ADDRBUS[2];
  //   memind = ADDRBUS[3]; postincr = ADDRBUS[4]; pcrelpom = ADDRBUS[5]; CLK = in_2; FCBUS = in_3;
  //   ST = INSTRUCBUS[16]; ADDR = PHASEFFBUS[1]; rst = in_1

  // Notes on the sheet:
  //   Operaciona jedinica
  //   Upravljacka jedinica
endmodule

module EXEC (
  input  [15:0] A,
  input  in_2,
  input  in_3,
  input  in_4,
  input  [15:0] B,
  input  [3:0] PHASEFFBUS,
  input  [19:0] INSTRUCBUS,
  input  [5:0] ADDRBUS,
  input  [15:0] PSW,
  output [15:0] ALU,
  output [14:0] CMEMBUS,
  output [7:0] CFFBUS,
  output [25:0] CREGBUS,
  output [5:0] CPSW,
  output rdMEM,
  output wrMEM
);

  wire and_2_out, and_3_out, and_4_out, and_5_out, and_6_out, and_7_out, and_8_out, and_9_out, and_10_out,
       and_11_out, and_12_out, and_13_out, and_t, brcnd, brnotbrorjmp, brnotEXEC, brnotFCBUS, bropr, brorjmp,
       brregdir, brsc16, brscn, bruncnd, C16, clEXEC, clPSWSTART, clSC, decA, decSC, decSP, incMAR, incSC,
       incSP, ldA, ldC, ldDWH, ldDWL, ldMAR, ldMDR, ldN, ldPC, ldSCN, ldV, ldZ, mxGPR0, mxGPR1, mxGPR2,
       mxMAR0, mxMAR2, mxMDR0, mxMDR1, mxMDR2, mxMDRGPR, mxSC1, mxSC2, not_1_out, not_2_out, not_3_out,
       not_4_out, not_5_out, not_t, or_1_out, or_2_out, or_3_out, rdMEM_t, SC16, SCN, slA, stINTR, sub_t,
       wrGPR, wrMEM_t, xor_1_out, xor_2_out;
  wire [3:0] dc4_16_1_p1;
  wire [4:0] reg5_cl_inc_1_p3;
  wire [5:0] kmopr6_1_adr5__0, mp2_6b_1_p3, reg6_inc_ld_1_a5__0;
  wire [6:0] reg8_1_p4;
  wire [7:0] rom64x48_1_dout;
  wire [24:19] mp2_6b_1_p2;

  // REG5_CL_INC reg5_cl_inc_1: pin names not known; wires that end beside it: clSC, in_3, reg5_cl_inc_1_p3, incSC
  // DC4_16 dc4_16_1: pin names not known; wires that end beside it: dc4_16_1_p1, 1'b1, bruncnd, brnotEXEC, brregdir, brnotbrorjmp, brsc16, brscn, brnotFCBUS, bropr
  and and_1 (SC16, reg5_cl_inc_1_p3[4], ~reg5_cl_inc_1_p3[3], ~reg5_cl_inc_1_p3[2], ~reg5_cl_inc_1_p3[1], ~reg5_cl_inc_1_p3[0]);  // AND_Gate
  KMOPR6 kmopr6_1 (
    .LD(INSTRUCBUS[15]), .ST(INSTRUCBUS[16]), .SUB(INSTRUCBUS[17]), .AND(INSTRUCBUS[18]),
    .NOT(INSTRUCBUS[19]), .BLSS(INSTRUCBUS[7]), .BNCR(INSTRUCBUS[8]), .BGRTU(INSTRUCBUS[9]),
    .BNEG(INSTRUCBUS[10]), .JLEQ(INSTRUCBUS[11]), .LOOPGRE(INSTRUCBUS[12]), .JMP(INSTRUCBUS[13]),
    .JSR(INSTRUCBUS[14]), .HALT(INSTRUCBUS[0]), .RTS(INSTRUCBUS[1]), .RTI(INSTRUCBUS[2]),
    .ASL(INSTRUCBUS[3]), .ROLC(INSTRUCBUS[4]), .PUSHGPR(INSTRUCBUS[5]), .POPGPR(INSTRUCBUS[6]),
    .Adr5__0(kmopr6_1_adr5__0));
  not not_1 (not_1_out, in_2);
  // REG8 reg8_1: pin names not known; wires that end beside it: 1'b0, in_3, 8'hf, {SCN, reg8_1_p4}, ldSCN, decSC
  // MP2_6b mp2_6b_1: pin names not known; wires that end beside it: bropr, mp2_6b_1_p2, mp2_6b_1_p3, kmopr6_1_adr5__0, 1'b1
  REG6_INC_LD reg6_inc_ld_1 (
    .I5__0(mp2_6b_1_p3), .LD(or_1_out), .INC(not_2_out), .mr(not_1_out), .CLK(in_3),
    .A5__0(reg6_inc_ld_1_a5__0));
  not not_2 (not_2_out, or_1_out);
  ROM64x48 rom64x48_1 (
    .A5__0(reg6_inc_ld_1_a5__0), .CS(1'b1),
    .DOUT_2({mp2_6b_1_p2, dc4_16_1_p1, clEXEC, stINTR, mxSC2, ldSCN, decSC, incSC, mxMDRGPR, mxSC1, clSC, ldC, slA, ldDWH, ldDWL, ldMAR, and_t}),
    .DOUT({rdMEM_t, incSP, clPSWSTART, mxGPR2, mxMDR2, mxMAR2, mxMAR0, decSP, decA, ldPC, not_t, mxGPR1, ldV, sub_t, mxGPR0, wrGPR, incMAR, mxMDR1, wrMEM_t, mxMDR0, ldMDR, ldZ, ldN, ldA, rom64x48_1_dout}));
  or or_1 (or_1_out, bruncnd, brcnd, bropr);
  ALU16 alu16_1 (.Cin(1'b0), .A(A), .B(B), .add(1'b0), .sub(sub_t), .NOT(not_t), .OR(and_t), .F(ALU), .Cout(C16));
  not not_3 (not_3_out, PHASEFFBUS[2]);
  not not_4 (not_4_out, brorjmp);
  not not_5 (not_5_out, in_4);
  xor xor_1 (xor_1_out, PSW[2], PSW[3]);
  xor xor_2 (xor_2_out, PSW[2], PSW[3]);
  and and_2 (and_2_out, not_3_out, brnotEXEC);
  and and_3 (and_3_out, SC16, brsc16);
  and and_4 (and_4_out, ADDRBUS[2], brregdir);
  and and_5 (and_5_out, not_4_out, brnotbrorjmp);
  and and_6 (and_6_out, not_5_out, brnotFCBUS);
  and and_7 (and_7_out, SCN, brscn);
  or or_2 (or_2_out, PSW[4], PSW[1]);
  or or_3 (or_3_out, xor_1_out, PSW[1]);
  and and_8 (and_8_out, ~xor_2_out, INSTRUCBUS[12]);  // AND_Gate
  and and_9 (and_9_out, xor_1_out, INSTRUCBUS[7]);
  and and_10 (and_10_out, ~PSW[4], INSTRUCBUS[8]);  // AND_Gate
  and and_11 (and_11_out, PSW[2], INSTRUCBUS[10]);
  and and_12 (and_12_out, ~or_2_out, INSTRUCBUS[9]);  // AND_Gate
  and and_13 (and_13_out, or_3_out, INSTRUCBUS[11]);
  or or_4 (brcnd, and_2_out, and_3_out, and_4_out, and_5_out, and_6_out, and_7_out);
  or or_5 (brorjmp, and_9_out, and_10_out, and_11_out, and_12_out, and_13_out, and_8_out);
  assign CMEMBUS[7] = mxMAR2 ? 1'b1 : 1'bz;  // Controlled_Buffer controlled_buffer_1
  assign CMEMBUS[8] = mxMDR0 ? 1'b1 : 1'bz;  // Controlled_Buffer controlled_buffer_2
  assign rdMEM = rdMEM_t ? 1'b1 : 1'bz;  // Controlled_Buffer controlled_buffer_3
  assign wrMEM = wrMEM_t ? 1'b1 : 1'bz;  // Controlled_Buffer controlled_buffer_4
  assign CMEMBUS[9] = mxMDR1 ? 1'b1 : 1'bz;  // Controlled_Buffer controlled_buffer_5
  assign CMEMBUS[11] = mxMDRGPR ? 1'b1 : 1'bz;  // Controlled_Buffer controlled_buffer_6
  assign CREGBUS[2] = ldDWL ? 1'b1 : 1'bz;  // Controlled_Buffer controlled_buffer_7
  assign CREGBUS[10] = decSP ? 1'b1 : 1'bz;  // Controlled_Buffer controlled_buffer_8
  assign CREGBUS[12] = clSC ? 1'b1 : 1'bz;  // Controlled_Buffer controlled_buffer_9
  assign CREGBUS[13] = mxSC1 ? 1'b1 : 1'bz;  // Controlled_Buffer controlled_buffer_10
  assign CREGBUS[14] = incSC ? 1'b1 : 1'bz;  // Controlled_Buffer controlled_buffer_11
  assign CREGBUS[15] = decSC ? 1'b1 : 1'bz;  // Controlled_Buffer controlled_buffer_12
  assign CREGBUS[16] = ldSCN ? 1'b1 : 1'bz;  // Controlled_Buffer controlled_buffer_13
  assign CREGBUS[17] = mxSC2 ? 1'b1 : 1'bz;  // Controlled_Buffer controlled_buffer_14
  assign CREGBUS[18] = mxGPR0 ? 1'b1 : 1'bz;  // Controlled_Buffer controlled_buffer_15
  assign CMEMBUS[3] = ldPC ? 1'b1 : 1'bz;  // Controlled_Buffer controlled_buffer_16
  assign CMEMBUS[5] = mxMAR0 ? 1'b1 : 1'bz;  // Controlled_Buffer controlled_buffer_17
  assign CMEMBUS[10] = mxMDR2 ? 1'b1 : 1'bz;  // Controlled_Buffer controlled_buffer_18
  assign CMEMBUS[14] = mxGPR2 ? 1'b1 : 1'bz;  // Controlled_Buffer controlled_buffer_19
  assign CREGBUS[1] = ldA ? 1'b1 : 1'bz;  // Controlled_Buffer controlled_buffer_20
  assign CREGBUS[11] = slA ? 1'b1 : 1'bz;  // Controlled_Buffer controlled_buffer_21
  assign CMEMBUS[2] = ldMDR ? 1'b1 : 1'bz;  // Controlled_Buffer controlled_buffer_22
  assign CREGBUS[3] = ldDWH ? 1'b1 : 1'bz;  // Controlled_Buffer controlled_buffer_23
  assign CMEMBUS[0] = ldMAR ? 1'b1 : 1'bz;  // Controlled_Buffer controlled_buffer_24
  assign CMEMBUS[1] = incMAR ? 1'b1 : 1'bz;  // Controlled_Buffer controlled_buffer_25
  assign CFFBUS[5] = clEXEC ? 1'b1 : 1'bz;  // Controlled_Buffer controlled_buffer_26
  assign CREGBUS[19] = mxGPR1 ? 1'b1 : 1'bz;  // Controlled_Buffer controlled_buffer_27
  assign CREGBUS[21] = wrGPR ? 1'b1 : 1'bz;  // Controlled_Buffer controlled_buffer_28
  assign CPSW[0] = clPSWSTART ? 1'b1 : 1'bz;  // Controlled_Buffer controlled_buffer_29
  assign CPSW[1] = ldZ ? 1'b1 : 1'bz;  // Controlled_Buffer controlled_buffer_30
  assign CPSW[2] = ldN ? 1'b1 : 1'bz;  // Controlled_Buffer controlled_buffer_31
  assign CPSW[3] = ldV ? 1'b1 : 1'bz;  // Controlled_Buffer controlled_buffer_32
  assign CPSW[4] = ldC ? 1'b1 : 1'bz;  // Controlled_Buffer controlled_buffer_33
  assign CFFBUS[6] = stINTR ? 1'b1 : 1'bz;  // Controlled_Buffer controlled_buffer_34
  assign CREGBUS[20] = mxGPR2 ? 1'b1 : 1'bz;  // Controlled_Buffer controlled_buffer_35
  assign CREGBUS[23] = decA ? 1'b1 : 1'bz;  // Controlled_Buffer controlled_buffer_36
  assign CREGBUS[24] = incSP ? 1'b1 : 1'bz;  // Controlled_Buffer controlled_buffer_37

  // Other names for the same wires on the sheet: A15__0[15:0] = A; regdir = ADDRBUS[2]; ALU15__0[15:0] = ALU;
  //   B15__0[15:0] = B; CLK = in_3; FCBUS = in_4; HALT = INSTRUCBUS[0]; RTS = INSTRUCBUS[1]; RTI = INSTRUCBUS[2];
  //   ASL = INSTRUCBUS[3]; ROLC = INSTRUCBUS[4]; PUSHGPR = INSTRUCBUS[5]; POPGPR = INSTRUCBUS[6];
  //   BLSS = INSTRUCBUS[7]; BNCR = INSTRUCBUS[8]; BGRTU = INSTRUCBUS[9]; BNEG = INSTRUCBUS[10]; JLEQ = INSTRUCBUS[11];
  //   LOOPGRE = INSTRUCBUS[12]; JMP = INSTRUCBUS[13]; JSR = INSTRUCBUS[14]; LD = INSTRUCBUS[15]; ST = INSTRUCBUS[16];
  //   SUB = INSTRUCBUS[17]; AND = INSTRUCBUS[18]; NOT = INSTRUCBUS[19]; EXEC = PHASEFFBUS[2]; PSWSTART = PSW[0];
  //   PSWZ = PSW[1]; PSWN = PSW[2]; PSWV = PSW[3]; PSWC = PSW[4]; rst = in_2

  // Notes on the sheet:
  //   Operaciona jedinica
  //   Upravljacka jedinica
  //   ALU
  //   Uslov za skok
endmodule

module INTR (
  input  in_1,
  input  in_2,
  input  in_3,
  input  [3:0] PHASEFFBUS,
  input  [19:0] INSTRUCBUS,
  input  [15:0] PSW,
  input  [3:0] intr,
  output [15:0] ADDIVTP,
  output [1:0] UEXT1__0,
  output inta,
  output [14:0] CMEMBUS,
  output [7:0] CFFBUS,
  output [25:0] CREGBUS,
  output rdMEM,
  output wrMEM
);

  wire and_2_out, and_3_out, and_4_out, brcnd, brnotFCBUS, brnotINTR, brnotprekid, bruncnd, clINTR, decSP,
       incMAR, ldDWH, ldDWL, ldMAR, ldMDR, ldPC, mxGPR0, mxGPR2, mxMAR0, mxMAR1, mxMAR2, mxMDR0, mxMDR1,
       mxMDR2, not_1_out, not_2_out, not_3_out, not_5_out, not_6_out, not_7_out, prekid, prper, rdMEM_t,
       reg5_cl_inc_ld_1_p5, reg5_cl_inc_ld_1_p6, stFETCH, wrMEM_t;
  wire [2:0] dc3_8_1_p1;
  wire [2:1] IVTDSP15__0;
  wire [4:0] reg5_cl_inc_ld_1_p3, reg5_cl_inc_ld_1_p4;
  wire [15:0] IVTP15__0;

  and and_1 (prekid, prper, PSW[15], not_2_out);
  not not_1 (not_1_out, in_1);
  // REG5_CL_INC_LD reg5_cl_inc_ld_1: pin names not known; wires that end beside it: in_2, not_1_out, reg5_cl_inc_ld_1_p3, reg5_cl_inc_ld_1_p4, reg5_cl_inc_ld_1_p5, reg5_cl_inc_ld_1_p6
  // DC3_8 dc3_8_1: pin names not known; wires that end beside it: dc3_8_1_p1, 1'b1, bruncnd, brnotINTR, brnotprekid, brnotFCBUS
  not not_2 (not_2_out, INSTRUCBUS[0]);
  not not_3 (not_3_out, in_1);
  // REG16_LD reg16_ld_1: pin names not known; wires that end beside it: in_2, not_3_out, IVTP15__0, 1'b0
  not not_4 (reg5_cl_inc_ld_1_p6, reg5_cl_inc_ld_1_p5);
  or or_1 (prper, intr[3], intr[2], intr[1], intr[0]);
  or or_2 (reg5_cl_inc_ld_1_p5, bruncnd, brcnd);
  ROM32x27 rom32x27_1 (
    .A4__0(reg5_cl_inc_ld_1_p4), .CS(1'b1),
    .DOUT({reg5_cl_inc_ld_1_p3, dc3_8_1_p1, clINTR, stFETCH, mxGPR2, mxGPR0, ldPC, ldDWH, rdMEM_t, ldDWL, incMAR, mxMAR1, inta, mxMDR2, wrMEM_t, mxMAR2, mxMAR0, ldMAR, mxMDR1, mxMDR0, ldMDR, decSP}));
  // CD4 cd4_1: pin names not known; wires that end beside it: intr[3], intr[2], intr[1], intr[0], 1'b1, UEXT1__0[1], UEXT1__0[0]
  // REG2_LD reg2_ld_1: pin names not known; wires that end beside it: in_2, UEXT1__0, IVTDSP15__0, inta
  // ADD16 add16_1: pin names not known; wires that end beside it: IVTP15__0, ADDIVTP, {{13{1'b0}}, IVTDSP15__0, 1'b0}, 1'b0
  not not_5 (not_5_out, PHASEFFBUS[3]);
  not not_6 (not_6_out, prekid);
  not not_7 (not_7_out, in_3);
  and and_2 (and_2_out, not_5_out, brnotINTR);
  and and_3 (and_3_out, not_6_out, brnotprekid);
  and and_4 (and_4_out, not_7_out, brnotFCBUS);
  or or_3 (brcnd, and_2_out, and_3_out, and_4_out);
  assign CMEMBUS[9] = mxMDR1 ? 1'b1 : 1'bz;  // Controlled_Buffer controlled_buffer_1
  assign CMEMBUS[10] = mxMDR2 ? 1'b1 : 1'bz;  // Controlled_Buffer controlled_buffer_2
  assign CMEMBUS[6] = mxMAR1 ? 1'b1 : 1'bz;  // Controlled_Buffer controlled_buffer_3
  assign CMEMBUS[7] = mxMAR2 ? 1'b1 : 1'bz;  // Controlled_Buffer controlled_buffer_4
  assign CMEMBUS[8] = mxMDR0 ? 1'b1 : 1'bz;  // Controlled_Buffer controlled_buffer_5
  assign CREGBUS[10] = decSP ? 1'b1 : 1'bz;  // Controlled_Buffer controlled_buffer_6
  assign CMEMBUS[0] = ldMAR ? 1'b1 : 1'bz;  // Controlled_Buffer controlled_buffer_7
  assign CMEMBUS[1] = incMAR ? 1'b1 : 1'bz;  // Controlled_Buffer controlled_buffer_8
  assign CMEMBUS[2] = ldMDR ? 1'b1 : 1'bz;  // Controlled_Buffer controlled_buffer_9
  assign CMEMBUS[3] = ldPC ? 1'b1 : 1'bz;  // Controlled_Buffer controlled_buffer_10
  assign CFFBUS[0] = stFETCH ? 1'b1 : 1'bz;  // Controlled_Buffer controlled_buffer_11
  assign CFFBUS[7] = clINTR ? 1'b1 : 1'bz;  // Controlled_Buffer controlled_buffer_12
  assign CREGBUS[2] = ldDWL ? 1'b1 : 1'bz;  // Controlled_Buffer controlled_buffer_13
  assign CREGBUS[3] = ldDWH ? 1'b1 : 1'bz;  // Controlled_Buffer controlled_buffer_14
  assign CREGBUS[18] = mxGPR0 ? 1'b1 : 1'bz;  // Controlled_Buffer controlled_buffer_15
  assign CREGBUS[20] = mxGPR2 ? 1'b1 : 1'bz;  // Controlled_Buffer controlled_buffer_16
  assign rdMEM = rdMEM_t ? 1'b1 : 1'bz;  // Controlled_Buffer controlled_buffer_17
  assign wrMEM = wrMEM_t ? 1'b1 : 1'bz;  // Controlled_Buffer controlled_buffer_18

  // Other names for the same wires on the sheet: ldBR = inta; ADDIVTP15__0[15:0] = ADDIVTP; CLK = in_2; FCBUS = in_3;
  //   HALT = INSTRUCBUS[0]; intr3__0[3:0] = intr; INTR_t = PHASEFFBUS[3]; PSWI = PSW[15]; rst = in_1

  // Notes on the sheet:
  //   Operaciona jedinica
  //   Upravljacka jedinica
endmodule

module RAM (
  input  [15:0] in_1,
  input  in_2,
  input  [7:0] in_3,
  input  in_4,
  input  in_5,
  input  in_6,
  output [7:0] out_7,
  output out_8
);

  wire and_1_out, and_2_out, CNT0, LDCNT, not_1_out, notCNT0, or_1_out, reg4_ld_sl_sr_1_p6, rsff_2_p4,
       rsff_2_p5, rsff_3_p4, sl;
  wire [3:0] CNT, LFSR;

  // RSFF rsff_1: pin names not known; wires that end beside it: 1'b0, in_2, in_6, sl
  or or_1 (or_1_out, in_4, in_5);
  // REG4_LD_SL_SR reg4_ld_sl_sr_1: pin names not known; wires that end beside it: 1'b0, 1'b0, in_2, 4'b1111, LFSR, reg4_ld_sl_sr_1_p6, sl, in_6
  // RisingEdge risingedge_1: pin names not known; wires that end beside it: or_1_out, in_2, LDCNT
  // MEM64Kx8 mem64kx8_1: pin names not known; wires that end beside it: in_1, 1'b1, in_2, in_3, out_7, in_4
  xor xor_1 (reg4_ld_sl_sr_1_p6, LFSR[2], LFSR[3]);
  and and_1 (and_1_out, CNT0, not_1_out);
  not not_1 (not_1_out, LDCNT);
  // RSFF rsff_2: pin names not known; wires that end beside it: and_1_out, in_2, LDCNT, rsff_2_p4, rsff_2_p5
  not not_2 (rsff_2_p4, in_6);
  and and_2 (and_2_out, rsff_2_p5, CNT0);
  // REG4m_DEC_LD reg4m_dec_ld_1: pin names not known; wires that end beside it: in_2, LFSR, CNT, LDCNT, notCNT0, notCNT0
  or or_2 (notCNT0, CNT[0], CNT[1], CNT[2], CNT[3]);
  // RSFF rsff_3: pin names not known; wires that end beside it: out_8, in_2, and_2_out, rsff_3_p4, out_8
  not not_3 (rsff_3_p4, in_6);
  not not_4 (CNT0, notCNT0);

  // Other names for the same wires on the sheet: ADR[15:0] = in_1; CLK = in_2; DIN[7:0] = in_3; DOUT[7:0] = out_7;
  //   fc = out_8; RDMEM = in_5; rst = in_6; WRMEM = in_4

  // Notes on the sheet:
  //   Random broj predstavlja vreme pristupa memoriji
  //   Brojac za generisanje random broja 
  //   Jedinica za generisanje function complete (fc) signala
  //   Brojac za dekrementiranje random broja
endmodule
