// Logisim project ETFStudent.circ as structural Verilog: 13 circuits, main circuit REG32_LD
module REG32_LD (
  input  [31:0] I15__0,
  input  LD,
  input  mr,
  input  CLK,
  output [31:0] A15__0
);

  // REG16_LD reg16_ld_1: pin names not known; wires that end beside it: CLK, mr, I15__0[31:16], A15__0[31:16], LD
  // REG16_LD reg16_ld_2: pin names not known; wires that end beside it: CLK, mr, I15__0[15:0], A15__0[15:0], LD

  // Notes on the sheet:
  //   __
endmodule

module KMADR (
  input  immed,
  input  memdir,
  input  regdir,
  input  regindpom,
  output [3:0] Adr3__0
);

  assign Adr3__0 = immed ? 4'b0010 : 4'bz;  // Controlled_Buffer controlled_buffer_1
  assign Adr3__0 = memdir ? 4'b0100 : 4'bz;  // Controlled_Buffer controlled_buffer_2
  assign Adr3__0 = regdir ? 4'b0101 : 4'bz;  // Controlled_Buffer controlled_buffer_3
  assign Adr3__0 = regindpom ? 4'b0111 : 4'bz;  // Controlled_Buffer controlled_buffer_4
endmodule

module KMOPR (
  input  LD,
  input  ST,
  input  ADD,
  input  SUB,
  input  BLSS,
  input  JLEQ,
  input  JMP,
  input  JSR,
  input  RTS,
  input  RTI,
  input  HALT,
  output [5:0] Adr5__0
);

  assign Adr5__0 = LD ? 6'b000010 : 6'bz;  // Controlled_Buffer controlled_buffer_1
  assign Adr5__0 = ST ? 6'b000100 : 6'bz;  // Controlled_Buffer controlled_buffer_2
  assign Adr5__0 = ADD ? 6'b001010 : 6'bz;  // Controlled_Buffer controlled_buffer_3
  assign Adr5__0 = SUB ? 6'b001100 : 6'bz;  // Controlled_Buffer controlled_buffer_4
  assign Adr5__0 = BLSS ? 6'b001110 : 6'bz;  // Controlled_Buffer controlled_buffer_5
  assign Adr5__0 = JLEQ ? 6'b010000 : 6'bz;  // Controlled_Buffer controlled_buffer_6
  assign Adr5__0 = JMP ? 6'b010001 : 6'bz;  // Controlled_Buffer controlled_buffer_7
  assign Adr5__0 = JSR ? 6'b010010 : 6'bz;  // Controlled_Buffer controlled_buffer_8
  assign Adr5__0 = RTS ? 6'b010111 : 6'bz;  // Controlled_Buffer controlled_buffer_9
  assign Adr5__0 = RTI ? 6'b011110 : 6'bz;  // Controlled_Buffer controlled_buffer_10
  assign Adr5__0 = HALT ? 6'b100010 : 6'bz;  // Controlled_Buffer controlled_buffer_11
endmodule

module REG6_INC_LD (
  input  [5:0] I5__0,
  input  LD,
  input  INC,
  input  mr,
  input  CLK,
  output [5:0] A5__0
);

  wire reg2m_inc_ld_1_p7, reg2m_inc_ld_2_p8;

  // REG2m_INC_LD reg2m_inc_ld_1: pin names not known; wires that end beside it: CLK, mr, I5__0[5:4], A5__0[5:4], LD, INC, reg2m_inc_ld_1_p7
  // REG2m_INC_LD reg2m_inc_ld_2: pin names not known; wires that end beside it: CLK, reg2m_inc_ld_1_p7, mr, I5__0[3:2], A5__0[3:2], LD, INC, reg2m_inc_ld_2_p8
  // REG2m_INC_LD reg2m_inc_ld_3: pin names not known; wires that end beside it: CLK, reg2m_inc_ld_2_p8, mr, I5__0[1:0], A5__0[1:0], LD, INC, INC

  // Notes on the sheet:
  //   __
endmodule

module ROM (
  input  [4:0] A4__0,
  input  CS,
  output [23:0] DOUT
);

  ROM_part #(.addrWidth(5), .dataWidth(24)) rom_1 (.addr(A4__0), .data(DOUT), .sel(CS));
endmodule

module GPR16x16 (
  input  [15:0] DI15__0,
  input  [3:0] A3__0,
  input  WR,
  input  CLK,
  output [15:0] DO15__0
);

  wire and_8_out, CS0, CS1, CS2, CS3, CS4, CS5, CS6, CS7, CS8, CS9, CS10, CS11, CS12, CS13, CS14, CS15,
       reg16_ld_1_p4, reg16_ld_2_p4, reg16_ld_3_p4, reg16_ld_4_p4, reg16_ld_5_p4, reg16_ld_6_p4,
       reg16_ld_7_p4, reg16_ld_9_p4, reg16_ld_10_p4, reg16_ld_11_p4, reg16_ld_12_p4, reg16_ld_13_p4,
       reg16_ld_14_p4, reg16_ld_15_p4, reg16_ld_16_p4;
  wire [15:0] reg16_ld_1_p3, reg16_ld_2_p3, reg16_ld_3_p3, reg16_ld_4_p3, reg16_ld_5_p3, reg16_ld_6_p3,
       reg16_ld_7_p3, reg16_ld_8_p3, reg16_ld_9_p3, reg16_ld_10_p3, reg16_ld_11_p3, reg16_ld_12_p3,
       reg16_ld_13_p3, reg16_ld_14_p3, reg16_ld_15_p3, reg16_ld_16_p3;

  // DC4_16 dc4_16_1: pin names not known; wires that end beside it: A3__0, 1'b1, CS0, CS1, CS2, CS3, CS4, CS5, CS6, CS7, CS8, CS9, CS10, CS11, CS12, CS13, CS14, CS15
  // REG16_LD reg16_ld_1: pin names not known; wires that end beside it: CLK, DI15__0, reg16_ld_1_p3, reg16_ld_1_p4
  assign DO15__0 = CS0 ? reg16_ld_1_p3 : 16'bz;  // Controlled_Buffer controlled_buffer_1
  // REG16_LD reg16_ld_2: pin names not known; wires that end beside it: CLK, DI15__0, reg16_ld_2_p3, reg16_ld_2_p4
  assign DO15__0 = CS1 ? reg16_ld_2_p3 : 16'bz;  // Controlled_Buffer controlled_buffer_2
  // REG16_LD reg16_ld_3: pin names not known; wires that end beside it: CLK, DI15__0, reg16_ld_3_p3, reg16_ld_3_p4
  assign DO15__0 = CS2 ? reg16_ld_3_p3 : 16'bz;  // Controlled_Buffer controlled_buffer_3
  // REG16_LD reg16_ld_4: pin names not known; wires that end beside it: CLK, DI15__0, reg16_ld_4_p3, reg16_ld_4_p4
  assign DO15__0 = CS3 ? reg16_ld_4_p3 : 16'bz;  // Controlled_Buffer controlled_buffer_4
  and and_1 (reg16_ld_1_p4, CS0, WR);
  and and_2 (reg16_ld_2_p4, CS1, WR);
  and and_3 (reg16_ld_3_p4, CS2, WR);
  and and_4 (reg16_ld_4_p4, CS3, WR);
  // REG16_LD reg16_ld_5: pin names not known; wires that end beside it: CLK, DI15__0, reg16_ld_5_p3, reg16_ld_5_p4
  and and_5 (reg16_ld_5_p4, CS4, WR);
  assign DO15__0 = CS4 ? reg16_ld_5_p3 : 16'bz;  // Controlled_Buffer controlled_buffer_5
  // REG16_LD reg16_ld_6: pin names not known; wires that end beside it: CLK, DI15__0, reg16_ld_6_p3, reg16_ld_6_p4
  and and_6 (reg16_ld_6_p4, CS5, WR);
  assign DO15__0 = CS5 ? reg16_ld_6_p3 : 16'bz;  // Controlled_Buffer controlled_buffer_6
  // REG16_LD reg16_ld_7: pin names not known; wires that end beside it: CLK, DI15__0, reg16_ld_7_p3, reg16_ld_7_p4
  and and_7 (reg16_ld_7_p4, CS6, WR);
  assign DO15__0 = CS6 ? reg16_ld_7_p3 : 16'bz;  // Controlled_Buffer controlled_buffer_7
  and and_8 (and_8_out, CS7, WR);
  // REG16_LD reg16_ld_8: pin names not known; wires that end beside it: CLK, DI15__0, reg16_ld_8_p3, and_8_out
  assign DO15__0 = CS7 ? reg16_ld_8_p3 : 16'bz;  // Controlled_Buffer controlled_buffer_8
  // REG16_LD reg16_ld_9: pin names not known; wires that end beside it: CLK, DI15__0, reg16_ld_9_p3, reg16_ld_9_p4
  assign DO15__0 = CS8 ? reg16_ld_9_p3 : 16'bz;  // Controlled_Buffer controlled_buffer_9
  // REG16_LD reg16_ld_10: pin names not known; wires that end beside it: CLK, DI15__0, reg16_ld_10_p3, reg16_ld_10_p4
  assign DO15__0 = CS9 ? reg16_ld_10_p3 : 16'bz;  // Controlled_Buffer controlled_buffer_10
  // REG16_LD reg16_ld_11: pin names not known; wires that end beside it: CLK, DI15__0, reg16_ld_11_p3, reg16_ld_11_p4
  assign DO15__0 = CS10 ? reg16_ld_11_p3 : 16'bz;  // Controlled_Buffer controlled_buffer_11
  // REG16_LD reg16_ld_12: pin names not known; wires that end beside it: CLK, DI15__0, reg16_ld_12_p3, reg16_ld_12_p4
  assign DO15__0 = CS11 ? reg16_ld_12_p3 : 16'bz;  // Controlled_Buffer controlled_buffer_12
  and and_9 (reg16_ld_9_p4, CS8, WR);
  and and_10 (reg16_ld_10_p4, CS9, WR);
  and and_11 (reg16_ld_11_p4, CS10, WR);
  and and_12 (reg16_ld_12_p4, CS11, WR);
  // REG16_LD reg16_ld_13: pin names not known; wires that end beside it: CLK, DI15__0, reg16_ld_13_p3, reg16_ld_13_p4
  assign DO15__0 = CS12 ? reg16_ld_13_p3 : 16'bz;  // Controlled_Buffer controlled_buffer_13
  // REG16_LD reg16_ld_14: pin names not known; wires that end beside it: CLK, DI15__0, reg16_ld_14_p3, reg16_ld_14_p4
  assign DO15__0 = CS13 ? reg16_ld_14_p3 : 16'bz;  // Controlled_Buffer controlled_buffer_14
  // REG16_LD reg16_ld_15: pin names not known; wires that end beside it: CLK, DI15__0, reg16_ld_15_p3, reg16_ld_15_p4
  assign DO15__0 = CS14 ? reg16_ld_15_p3 : 16'bz;  // Controlled_Buffer controlled_buffer_15
  // REG16_LD reg16_ld_16: pin names not known; wires that end beside it: CLK, DI15__0, reg16_ld_16_p3, reg16_ld_16_p4
  assign DO15__0 = CS15 ? reg16_ld_16_p3 : 16'bz;  // Controlled_Buffer controlled_buffer_16
  and and_13 (reg16_ld_13_p4, CS12, WR);
  and and_14 (reg16_ld_14_p4, CS13, WR);
  and and_15 (reg16_ld_15_p4, CS14, WR);
  and and_16 (reg16_ld_16_p4, CS15, WR);

  // Other names for the same wires on the sheet: inREG[15:0] = DI15__0; outREG[15:0] = DO15__0
endmodule

module KMADR5 (
  input  immed,
  input  memdir,
  input  regdir,
  input  memind,
  input  postincr,
  input  pcrelpom,
  output [4:0] Adr4__0
);

  assign Adr4__0 = immed ? 5'b00010 : 5'bz;  // Controlled_Buffer controlled_buffer_1
  assign Adr4__0 = memdir ? 5'b00011 : 5'bz;  // Controlled_Buffer controlled_buffer_2
  assign Adr4__0 = memind ? 5'b00110 : 5'bz;  // Controlled_Buffer controlled_buffer_3
  assign Adr4__0 = regdir ? 5'b00100 : 5'bz;  // Controlled_Buffer controlled_buffer_4
  assign Adr4__0 = postincr ? 5'b01101 : 5'bz;  // Controlled_Buffer controlled_buffer_5
  assign Adr4__0 = pcrelpom ? 5'b10001 : 5'bz;  // Controlled_Buffer controlled_buffer_6
endmodule

module GPR16x16N (
  input  [15:0] DI15__0,
  input  [3:0] A3__0,
  input  WR,
  input  CLK,
  input  incPC,
  input  rst,
  input  incSP,
  input  decSP,
  input  decA,
  input  slA,
  input  rolcA,
  input  C,
  output [15:0] DO15__0,
  output [15:0] DO15__0_2,
  output [15:0] DO15__0_3,
  output [15:0] DO15__0_4
);

  wire and_1_out, and_2_out, and_3_out, and_6_out, and_7_out, and_14_out, and_16_out, CS0, CS1, CS2, CS3,
       CS4, CS5, CS6, CS7, CS8, CS9, CS10, CS11, CS12, CS13, CS14, CS15, mp2_16b_1_p3, mp2_16b_2_p3,
       mp2_16b_3_p3, reg16_1_p4, reg16_1_p6, reg16_2_p4, reg16_inc_ld_1_p4, reg16_ld_1_p4, reg16_ld_2_p4,
       reg16_ld_5_p4, reg16_ld_6_p4, reg16_ld_7_p4, reg16_ld_8_p4, reg16_ld_9_p4, reg16_ld_10_p4,
       reg16_ld_12_p4;
  wire [15:0] reg16_ld_1_p3, reg16_ld_2_p3, reg16_ld_3_p3, reg16_ld_4_p3, reg16_ld_5_p3, reg16_ld_6_p3,
       reg16_ld_7_p3, reg16_ld_8_p3, reg16_ld_9_p3, reg16_ld_10_p3, reg16_ld_11_p3, reg16_ld_12_p3,
       reg16_ld_13_p3;

  // DC4_16 dc4_16_1: pin names not known; wires that end beside it: A3__0, 1'b1, CS0, CS1, CS2, CS3, CS4, CS5, CS6, CS7, CS8, CS9, CS10, CS11, CS12, CS13, CS14, CS15
  // MP2_16b mp2_16b_1: pin names not known; wires that end beside it: rst, DI15__0, mp2_16b_1_p3, 16'h1000
  // REG16_INC_LD reg16_inc_ld_1: pin names not known; wires that end beside it: CLK, mp2_16b_1_p3, DO15__0_2, reg16_inc_ld_1_p4, incPC
  assign DO15__0 = CS2 ? DO15__0_2 : 16'bz;  // Controlled_Buffer controlled_buffer_1
  and and_1 (and_1_out, CS2, WR);
  or or_1 (reg16_inc_ld_1_p4, and_1_out, rst);
  // MP2_16b mp2_16b_2: pin names not known; wires that end beside it: rst, DI15__0, mp2_16b_2_p3, {16{1'b0}}
  // REG16 reg16_1: pin names not known; wires that end beside it: CLK, mp2_16b_2_p3, DO15__0_3, reg16_1_p4, slA, reg16_1_p6, decA
  assign DO15__0 = CS0 ? DO15__0_3 : 16'bz;  // Controlled_Buffer controlled_buffer_2
  // MP2_16b mp2_16b_3: pin names not known; wires that end beside it: rst, DI15__0, mp2_16b_3_p3, 16'hf000
  // REG16 reg16_2: pin names not known; wires that end beside it: CLK, mp2_16b_3_p3, DO15__0_4, reg16_2_p4, incSP, decSP
  assign DO15__0 = CS1 ? DO15__0_4 : 16'bz;  // Controlled_Buffer controlled_buffer_3
  or or_2 (reg16_1_p4, rst, and_3_out);
  or or_3 (reg16_2_p4, rst, and_2_out);
  // MP2_1b mp2_1b_1: pin names not known; wires that end beside it: rolcA, 1'b0, reg16_1_p6, C, 1'b1
  and and_2 (and_2_out, CS1, WR);
  and and_3 (and_3_out, CS0, WR);
  // REG16_LD reg16_ld_1: pin names not known; wires that end beside it: CLK, DI15__0, reg16_ld_1_p3, reg16_ld_1_p4
  assign DO15__0 = CS3 ? reg16_ld_1_p3 : 16'bz;  // Controlled_Buffer controlled_buffer_4
  and and_4 (reg16_ld_1_p4, CS3, WR);
  // REG16_LD reg16_ld_2: pin names not known; wires that end beside it: CLK, DI15__0, reg16_ld_2_p3, reg16_ld_2_p4
  and and_5 (reg16_ld_2_p4, CS4, WR);
  assign DO15__0 = CS4 ? reg16_ld_2_p3 : 16'bz;  // Controlled_Buffer controlled_buffer_5
  and and_6 (and_6_out, CS5, WR);
  // REG16_LD reg16_ld_3: pin names not known; wires that end beside it: CLK, DI15__0, reg16_ld_3_p3, and_6_out
  assign DO15__0 = CS5 ? reg16_ld_3_p3 : 16'bz;  // Controlled_Buffer controlled_buffer_6
  and and_7 (and_7_out, CS6, WR);
  // REG16_LD reg16_ld_4: pin names not known; wires that end beside it: CLK, DI15__0, reg16_ld_4_p3, and_7_out
  assign DO15__0 = CS6 ? reg16_ld_4_p3 : 16'bz;  // Controlled_Buffer controlled_buffer_7
  // REG16_LD reg16_ld_5: pin names not known; wires that end beside it: CLK, DI15__0, reg16_ld_5_p3, reg16_ld_5_p4
  and and_8 (reg16_ld_5_p4, CS7, WR);
  assign DO15__0 = CS7 ? reg16_ld_5_p3 : 16'bz;  // Controlled_Buffer controlled_buffer_8
  // REG16_LD reg16_ld_6: pin names not known; wires that end beside it: CLK, DI15__0, reg16_ld_6_p3, reg16_ld_6_p4
  assign DO15__0 = CS8 ? reg16_ld_6_p3 : 16'bz;  // Controlled_Buffer controlled_buffer_9
  // REG16_LD reg16_ld_7: pin names not known; wires that end beside it: CLK, DI15__0, reg16_ld_7_p3, reg16_ld_7_p4
  assign DO15__0 = CS9 ? reg16_ld_7_p3 : 16'bz;  // Controlled_Buffer controlled_buffer_10
  // REG16_LD reg16_ld_8: pin names not known; wires that end beside it: CLK, DI15__0, reg16_ld_8_p3, reg16_ld_8_p4
  assign DO15__0 = CS10 ? reg16_ld_8_p3 : 16'bz;  // Controlled_Buffer controlled_buffer_11
  // REG16_LD reg16_ld_9: pin names not known; wires that end beside it: CLK, DI15__0, reg16_ld_9_p3, reg16_ld_9_p4
  assign DO15__0 = CS11 ? reg16_ld_9_p3 : 16'bz;  // Controlled_Buffer controlled_buffer_12
  and and_9 (reg16_ld_6_p4, CS8, WR);
  and and_10 (reg16_ld_7_p4, CS9, WR);
  and and_11 (reg16_ld_8_p4, CS10, WR);
  and and_12 (reg16_ld_9_p4, CS11, WR);
  // REG16_LD reg16_ld_10: pin names not known; wires that end beside it: CLK, DI15__0, reg16_ld_10_p3, reg16_ld_10_p4
  and and_13 (reg16_ld_10_p4, CS12, WR);
  assign DO15__0 = CS12 ? reg16_ld_10_p3 : 16'bz;  // Controlled_Buffer controlled_buffer_13
  and and_14 (and_14_out, CS13, WR);
  // REG16_LD reg16_ld_11: pin names not known; wires that end beside it: CLK, DI15__0, reg16_ld_11_p3, and_14_out
  assign DO15__0 = CS13 ? reg16_ld_11_p3 : 16'bz;  // Controlled_Buffer controlled_buffer_14
  // REG16_LD reg16_ld_12: pin names not known; wires that end beside it: CLK, DI15__0, reg16_ld_12_p3, reg16_ld_12_p4
  and and_15 (reg16_ld_12_p4, CS14, WR);
  assign DO15__0 = CS14 ? reg16_ld_12_p3 : 16'bz;  // Controlled_Buffer controlled_buffer_15
  and and_16 (and_16_out, CS15, WR);
  // REG16_LD reg16_ld_13: pin names not known; wires that end beside it: CLK, DI15__0, reg16_ld_13_p3, and_16_out
  assign DO15__0 = CS15 ? reg16_ld_13_p3 : 16'bz;  // Controlled_Buffer controlled_buffer_16

  // Other names for the same wires on the sheet: A15__0[15:0] = DO15__0_3; inREG[15:0] = DI15__0;
  //   outREG[15:0] = DO15__0; PC15__0[15:0] = DO15__0_2; SP15__0[15:0] = DO15__0_4
endmodule

module ALU16 (
  input  Cin,
  input  [15:0] A,
  input  [15:0] B,
  input  add,
  input  sub,
  input  NOT,
  input  OR,
  output [15:0] F,
  output Cout
);

  wire adder_1_cout, subtractor_1_bout;
  wire [15:0] adder_1_out, and_1_out, negator_1_out, subtractor_1_out;

  Negator #(.width(16)) negator_1 (.in(A), .out(negator_1_out));
  Adder #(.width(16)) adder_1 (.a(A), .b(B), .out(adder_1_out), .cin(Cin), .cout(adder_1_cout));
  Subtractor #(.width(16)) subtractor_1 (.a(A), .b(B), .out(subtractor_1_out), .bin(Cin), .bout(subtractor_1_bout));
  assign and_1_out = A & B;  // AND_Gate and_1, 16 bits wide
  assign F = add ? adder_1_out : 16'bz;  // Controlled_Buffer controlled_buffer_1
  assign Cout = add ? adder_1_cout : 1'bz;  // Controlled_Buffer controlled_buffer_2
  assign F = sub ? subtractor_1_out : 16'bz;  // Controlled_Buffer controlled_buffer_3
  assign Cout = sub ? subtractor_1_bout : 1'bz;  // Controlled_Buffer controlled_buffer_4
  assign F = NOT ? negator_1_out : 16'bz;  // Controlled_Buffer controlled_buffer_5
  assign F = OR ? and_1_out : 16'bz;  // Controlled_Buffer controlled_buffer_6
endmodule

module KMOPR6 (
  input  LD,
  input  ST,
  input  SUB,
  input  AND,
  input  NOT,
  input  BLSS,
  input  BNCR,
  input  BGRTU,
  input  BNEG,
  input  JLEQ,
  input  LOOPGRE,
  input  JMP,
  input  JSR,
  input  HALT,
  input  RTS,
  input  RTI,
  input  ASL,
  input  ROLC,
  input  PUSHGPR,
  input  POPGPR,
  output [5:0] Adr5__0
);

  assign Adr5__0 = LD ? 6'b000010 : 6'bz;  // Controlled_Buffer controlled_buffer_1
  assign Adr5__0 = ST ? 6'b000100 : 6'bz;  // Controlled_Buffer controlled_buffer_2
  assign Adr5__0 = SUB ? 6'b001011 : 6'bz;  // Controlled_Buffer controlled_buffer_3
  assign Adr5__0 = AND ? 6'b001101 : 6'bz;  // Controlled_Buffer controlled_buffer_4
  assign Adr5__0 = NOT ? 6'b001111 : 6'bz;  // Controlled_Buffer controlled_buffer_5
  assign Adr5__0 = BLSS ? 6'b010001 : 6'bz;  // Controlled_Buffer controlled_buffer_6
  assign Adr5__0 = BNCR ? 6'b010001 : 6'bz;  // Controlled_Buffer controlled_buffer_7
  assign Adr5__0 = BGRTU ? 6'b010001 : 6'bz;  // Controlled_Buffer controlled_buffer_8
  assign Adr5__0 = BNEG ? 6'b010001 : 6'bz;  // Controlled_Buffer controlled_buffer_9
  assign Adr5__0 = JLEQ ? 6'b111100 : 6'bz;  // Controlled_Buffer controlled_buffer_10
  assign Adr5__0 = LOOPGRE ? 6'b010011 : 6'bz;  // Controlled_Buffer controlled_buffer_11
  assign Adr5__0 = JMP ? 6'b010110 : 6'bz;  // Controlled_Buffer controlled_buffer_12
  assign Adr5__0 = JSR ? 6'b010111 : 6'bz;  // Controlled_Buffer controlled_buffer_13
  assign Adr5__0 = HALT ? 6'b011101 : 6'bz;  // Controlled_Buffer controlled_buffer_14
  assign Adr5__0 = RTI ? 6'b100100 : 6'bz;  // Controlled_Buffer controlled_buffer_15
  assign Adr5__0 = RTS ? 6'b011110 : 6'bz;  // Controlled_Buffer controlled_buffer_16
  assign Adr5__0 = ASL ? 6'b101010 : 6'bz;  // Controlled_Buffer controlled_buffer_17
  assign Adr5__0 = ROLC ? 6'b101011 : 6'bz;  // Controlled_Buffer controlled_buffer_18
  assign Adr5__0 = PUSHGPR ? 6'b101100 : 6'bz;  // Controlled_Buffer controlled_buffer_19
  assign Adr5__0 = POPGPR ? 6'b110100 : 6'bz;  // Controlled_Buffer controlled_buffer_20
endmodule

module ROM64x48 (
  input  [5:0] A5__0,
  input  CS,
  output [31:0] DOUT,
  output [24:0] DOUT_2
);

  ROM_part #(.addrWidth(6), .dataWidth(25)) rom_1 (.addr(A5__0), .data(DOUT_2), .sel(CS));
  ROM_part #(.addrWidth(6), .dataWidth(32)) rom_2 (.addr(A5__0), .data(DOUT), .sel(CS));
endmodule

module ROM32x27 (
  input  [4:0] A4__0,
  input  CS,
  output [27:0] DOUT
);

  ROM_part #(.addrWidth(5), .dataWidth(28)) rom_1 (.addr(A4__0), .data(DOUT), .sel(CS));
endmodule

module ROM32x24 (
  input  [4:0] A4__0,
  input  CS,
  output [23:0] DOUT
);

  ROM_part #(.addrWidth(5), .dataWidth(24)) rom_1 (.addr(A4__0), .data(DOUT), .sel(CS));
endmodule
